# Fritzing sketch Harvesting_System_Circuit_Diagram (saved by Fritzing 0.9.10b)
breadboards: 1

parts:
  Mod1 = Raspberry Pi 4B
  Part2 = Adafruit ADS1115 16Bit I2C ADC [part_number="Adafruit #1085"]
  Part3 = Thumb Joystick
  A1 = 2 channel relay module [package=THT]
  LED1 = LED - 5mm [color="Red (633nm)" current=0.030 package="5 mm [THT]"]
  R1 = Resistor [tolerance=±5% power=0.25 resistance=330 package=THT]
  L2 = Solenoid
  U1 = mystery part, 2 pins [chip_label=DC]
  L3 = Solenoid
  U2 = mystery part, 2 pins [chip_label=DC]

nets:
  3V3: Mod1.3V3, Part2.VDD, Part3.VRy
  N1: Mod1.GPIO2, Part2.SDA
  N2: Mod1.5V, A1.pin_13
  N3: Mod1.GPIO3, Part2.SCL
  GND: Mod1.GND, Mod1.GPIO4, Part2.GND, Part3.SW, A1.pin_14, R1.Pin_0
  N4: Mod1.GPIO23, LED1.anode
  N5: Mod1.GPIO24, Part3.GND
  N6: Mod1.GPIO20, A1.pin_16
  N7: Mod1.GPIO21, A1.pin_15
  N8: Part2.AIN1, Part3.+5V
  N9: Part2.AIN0, Part3.VRx
  N10: A1.pin_1, U1.pin2
  N11: A1.pin_2, L2.pin1
  N12: A1.pin_4, U2.pin2
  N13: A1.pin_5, L3.pin1
  N14: LED1.cathode, R1.Pin_1
  N15: L2.pin2, U1.pin1
  N16: L3.pin2, U2.pin1

custom parts:
  Adafruit ADS1115 16Bit I2C ADC: For microcontrollers without an analog-to-digital converter or when you want a higher-precision ADC, the ADS1115 provides 16-bit precision at 860 samples/second over I2C. The chip can be configured as 4 single-ended input channels, or two differential channels. As a nice bonus, it even includes a programmable gain amplifier, up to x16, to help boost up smaller single/differential signals to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
  Thumb Joystick: Description: This is the breakout board for the thumb joystick. Pins are broken out to a 0.1" header and includes 4 mounting holes in the corners. Dimensions: 1" x 1.25"
  2 channel relay module: 2 channel Relay Module 5V 12V 24V High and Low Level Trigger Relay Control With Optocoupler Two Way relays DC 5 V 12 V 24 V Volt.
